// Logisim project lab2.circ as structural Verilog: 1 circuit, main circuit main
module main (
  input  A0,
  input  A1,
  input  A2,
  input  A3,
  input  A4,
  input  A5,
  input  A6,
  output O0,
  output Z,
  output Z_2,
  output O1,
  output O2,
  output O3,
  output E,
  output G,
  output L,
  output I
);

  wire and_1_out, and_2_out, and_3_out, and_4_out, and_5_out, and_6_out, and_7_out, and_8_out, and_9_out,
       and_10_out, and_11_out, and_12_out, and_13_out, and_14_out, and_15_out, and_16_out, and_17_out,
       and_18_out, and_19_out, and_20_out, and_21_out, and_22_out, and_23_out, and_24_out, and_25_out,
       and_26_out, and_27_out, and_28_out, and_29_out, and_30_out, and_31_out, and_32_out, and_33_out,
       and_34_out, and_35_out, and_36_out, and_37_out, n3_to_8_decoder_74138_1_p8,
       n3_to_8_decoder_74138_1_p9, n3_to_8_decoder_74138_1_p10, n3_to_8_decoder_74138_1_p11,
       n3_to_8_decoder_74138_1_p12, n3_to_8_decoder_74138_1_p13, n3_to_8_decoder_74138_1_p14,
       n3_to_8_decoder_74138_1_p15, n4_to_1_mux_x2_74153_1_p13, n4_to_1_mux_x2_74153_1_p14,
       n4_to_1_mux_x2_74153_2_p13, n4_to_1_mux_x2_74153_2_p14, n4_to_1_mux_x2_74153_3_p13,
       n4_to_1_mux_x2_74153_3_p14, n4_to_1_mux_x2_74153_4_p13, n4_to_1_mux_x2_74153_4_p14,
       n4_to_1_mux_x2_74153_5_p13, n4_to_1_mux_x2_74153_5_p14, n4_to_1_mux_x2_74153_6_p13,
       n4_to_1_mux_x2_74153_6_p14, n4_to_1_mux_x2_74153_7_p13, n4_to_1_mux_x2_74153_7_p14,
       n4_to_1_mux_x2_74153_8_p13, n4_to_1_mux_x2_74153_8_p14, n4_to_1_mux_x2_74153_9_p1,
       n4_to_1_mux_x2_74153_9_p13, n4_to_1_mux_x2_74153_9_p17, n4_to_1_mux_x2_74153_9_p18, nor_1_out,
       nor_2_out, nor_3_out, not_1_out, not_2_out, not_3_out, not_4_out, not_8_out, not_9_out, not_10_out,
       not_11_out, not_12_out, not_13_out, not_14_out, not_15_out, not_16_out, not_17_out, not_18_out,
       not_19_out, not_20_out, not_21_out, or_1_out, or_2_out, or_3_out, or_4_out, or_5_out, or_14_out,
       xor_1_out, xor_2_out, xor_3_out, xor_4_out, xor_5_out, xor_6_out, xor_7_out, xor_8_out, xor_9_out,
       xor_10_out, xor_11_out, xor_12_out, xor_13_out, xor_14_out, xor_15_out, xor_16_out, xor_17_out,
       xor_18_out, xor_19_out;

  not not_1 (not_1_out, A0);
  not not_2 (not_2_out, A1);
  not not_3 (not_3_out, A2);
  not not_4 (not_4_out, A3);
  // NOT_Gate not_5 has open pins: in=A4, out=open
  // NOT_Gate not_6 has open pins: in=A5, out=open
  // NOT_Gate not_7 has open pins: in=A6, out=open
  xor xor_1 (xor_1_out, A1, A3);
  not not_8 (not_8_out, xor_1_out);
  not not_9 (not_9_out, xor_2_out);
  xor xor_2 (xor_2_out, A0, A2);
  not not_10 (not_10_out, xor_3_out);
  xor xor_3 (xor_3_out, A1, A3);
  and and_1 (and_1_out, not_1_out, A2);
  and and_2 (and_2_out, A0, A3);
  and and_3 (and_3_out, A1, A2);
  and and_4 (and_4_out, A1, A3);
  nor nor_1 (nor_1_out, A0, A1);
  nor nor_2 (nor_2_out, A2, A3);
  not not_11 (not_11_out, A1);
  xor xor_4 (xor_4_out, A1, A3);
  not not_12 (not_12_out, A2);
  xor xor_5 (xor_5_out, A1, A2);
  and and_5 (and_5_out, A2, not_4_out);
  // _3_to_8_decoder__74138 #(.Facing("east")) 3_to_8_decoder_74138_1: pin names not known; wires that end beside it: A6, A4, A5, A6, 1'b1, 1'b0, 1'b0, n3_to_8_decoder_74138_1_p8, n3_to_8_decoder_74138_1_p9, n3_to_8_decoder_74138_1_p10, n3_to_8_decoder_74138_1_p11, n3_to_8_decoder_74138_1_p12, n3_to_8_decoder_74138_1_p13, n3_to_8_decoder_74138_1_p14, n3_to_8_decoder_74138_1_p15
  and and_6 (and_6_out, A3, A1);
  and and_7 (and_7_out, A0, not_3_out);
  and and_8 (and_8_out, not_4_out, A1);
  xor xor_6 (xor_6_out, A1, A3);
  and and_9 (and_9_out, not_8_out, not_9_out);
  and and_10 (and_10_out, not_2_out, A3);
  and and_11 (and_11_out, not_10_out, and_1_out);
  xor xor_7 (xor_7_out, and_2_out, and_3_out);
  and and_12 (and_12_out, and_2_out, and_3_out);
  or or_1 (or_1_out, nor_1_out, nor_2_out);
  and and_13 (and_13_out, not_11_out, A3);
  not not_13 (not_13_out, xor_4_out);
  and and_14 (and_14_out, not_2_out, not_1_out);
  and and_15 (and_15_out, not_4_out, not_3_out);
  xor xor_8 (xor_8_out, A0, A2);
  xor xor_9 (xor_9_out, A1, A3);
  and and_16 (and_16_out, and_7_out, not_14_out);
  not not_14 (not_14_out, xor_6_out);
  or or_2 (or_2_out, and_10_out, and_11_out);
  xor xor_10 (xor_10_out, and_12_out, and_4_out);
  xor xor_11 (xor_11_out, A3, A2);
  and and_17 (and_17_out, not_13_out, and_18_out);
  and and_18 (and_18_out, A0, not_12_out);
  xor xor_12 (xor_12_out, A0, A1);
  xor xor_13 (xor_13_out, A1, A3);
  and and_19 (and_19_out, A0, A2);
  and and_20 (and_20_out, and_19_out, xor_9_out);
  or or_3 (or_3_out, and_20_out, and_6_out);
  or or_4 (or_4_out, and_16_out, and_8_out);
  or or_5 (or_5_out, and_13_out, and_17_out);
  and and_21 (and_21_out, and_14_out, and_15_out);
  xor xor_14 (xor_14_out, xor_13_out, and_19_out);
  and and_22 (and_22_out, n3_to_8_decoder_74138_1_p8, n3_to_8_decoder_74138_1_p9);
  and and_23 (and_23_out, n3_to_8_decoder_74138_1_p10, n3_to_8_decoder_74138_1_p11);
  not not_15 (not_15_out, A2);
  xor xor_15 (xor_15_out, A1, A0);
  and and_24 (and_24_out, and_22_out, and_23_out);
  and and_25 (and_25_out, n3_to_8_decoder_74138_1_p12, n3_to_8_decoder_74138_1_p13);
  and and_26 (and_26_out, A0, A1);
  xor xor_16 (xor_16_out, and_26_out, A2);
  xor xor_17 (xor_17_out, A1, A3);
  not not_16 (not_16_out, xor_17_out);
  xor xor_18 (xor_18_out, A2, A0);
  and and_27 (and_27_out, A2, A3);
  and and_28 (and_28_out, A0, A2);
  and and_29 (and_29_out, A3, not_15_out);
  and and_30 (and_30_out, A3, A2);
  and and_31 (and_31_out, n3_to_8_decoder_74138_1_p14, n3_to_8_decoder_74138_1_p15);
  not not_17 (not_17_out, xor_18_out);
  and and_32 (and_32_out, and_27_out, and_33_out);
  and and_33 (and_33_out, A0, A1);
  and and_34 (and_34_out, and_25_out, and_31_out);
  and and_35 (and_35_out, and_26_out, A2);
  xor xor_19 (xor_19_out, and_35_out, A3);
  not not_18 (not_18_out, and_9_out);
  not not_19 (not_19_out, or_5_out);
  and and_36 (and_36_out, not_18_out, not_19_out);
  // _4_to_1_MUX__x2___74153 #(.Facing("east")) 4_to_1_mux_x2_74153_1: pin names not known; wires that end beside it: xor_8_out, 1'b0, not_1_out, not_17_out, and_15_out, and_28_out, 1'b0, xor_12_out, and_24_out, A4, and_34_out, A5, n4_to_1_mux_x2_74153_1_p13, n4_to_1_mux_x2_74153_1_p14
  // _4_to_1_MUX__x2___74153 #(.Facing("east")) 4_to_1_mux_x2_74153_2: pin names not known; wires that end beside it: xor_14_out, 1'b0, xor_15_out, not_16_out, and_5_out, xor_7_out, 1'b0, xor_5_out, and_24_out, A4, and_34_out, A5, n4_to_1_mux_x2_74153_2_p13, n4_to_1_mux_x2_74153_2_p14
  // _4_to_1_MUX__x2___74153 #(.Facing("east")) 4_to_1_mux_x2_74153_3: pin names not known; wires that end beside it: or_3_out, 1'b0, xor_16_out, 1'b0, and_29_out, xor_10_out, 1'b0, xor_11_out, and_24_out, A4, and_34_out, A5, n4_to_1_mux_x2_74153_3_p13, n4_to_1_mux_x2_74153_3_p14, O2
  // _4_to_1_MUX__x2___74153 #(.Facing("east")) 4_to_1_mux_x2_74153_4: pin names not known; wires that end beside it: 1'b0, 1'b0, xor_19_out, 1'b0, and_30_out, and_12_out, 1'b0, A3, and_24_out, A4, and_34_out, A5, n4_to_1_mux_x2_74153_4_p13, n4_to_1_mux_x2_74153_4_p14
  // _4_to_1_MUX__x2___74153 #(.Facing("east")) 4_to_1_mux_x2_74153_5: pin names not known; wires that end beside it: 1'b0, and_9_out, 1'b0, 1'b0, 1'b0, 1'b0, and_9_out, 1'b0, and_24_out, A4, and_34_out, A5, n4_to_1_mux_x2_74153_5_p13, n4_to_1_mux_x2_74153_5_p14
  // _4_to_1_MUX__x2___74153 #(.Facing("east")) 4_to_1_mux_x2_74153_6: pin names not known; wires that end beside it: 1'b0, or_2_out, 1'b0, 1'b0, 1'b0, 1'b0, and_36_out, 1'b0, and_24_out, A4, and_34_out, A5, n4_to_1_mux_x2_74153_6_p13, n4_to_1_mux_x2_74153_6_p14
  // _4_to_1_MUX__x2___74153 #(.Facing("east")) 4_to_1_mux_x2_74153_7: pin names not known; wires that end beside it: 1'b0, or_4_out, 1'b0, 1'b0, 1'b0, 1'b0, or_5_out, 1'b0, and_24_out, A4, and_34_out, A5, n4_to_1_mux_x2_74153_7_p13, n4_to_1_mux_x2_74153_7_p14
  // _4_to_1_MUX__x2___74153 #(.Facing("east")) 4_to_1_mux_x2_74153_8: pin names not known; wires that end beside it: 1'b0, 1'b0, and_32_out, 1'b0, 1'b0, 1'b0, 1'b0, 1'b0, and_24_out, A4, and_34_out, A5, n4_to_1_mux_x2_74153_8_p13, n4_to_1_mux_x2_74153_8_p14
  or or_6 (O0, n4_to_1_mux_x2_74153_1_p13, n4_to_1_mux_x2_74153_1_p14);
  not not_20 (not_20_out, xor_8_out);
  not not_21 (not_21_out, xor_14_out);
  or or_7 (O1, n4_to_1_mux_x2_74153_2_p13, n4_to_1_mux_x2_74153_2_p14);
  or or_8 (O2, n4_to_1_mux_x2_74153_3_p13, n4_to_1_mux_x2_74153_3_p14);
  or or_9 (O3, n4_to_1_mux_x2_74153_4_p13, n4_to_1_mux_x2_74153_4_p14);
  or or_10 (E, n4_to_1_mux_x2_74153_5_p13, n4_to_1_mux_x2_74153_5_p14);
  or or_11 (G, n4_to_1_mux_x2_74153_6_p13, n4_to_1_mux_x2_74153_6_p14);
  or or_12 (L, n4_to_1_mux_x2_74153_7_p13, n4_to_1_mux_x2_74153_7_p14);
  or or_13 (I, n4_to_1_mux_x2_74153_8_p13, n4_to_1_mux_x2_74153_8_p14);
  and and_37 (and_37_out, not_20_out, not_21_out);
  or or_14 (or_14_out, xor_8_out, xor_14_out);
  nor nor_3 (nor_3_out, or_14_out, or_3_out);
  // _4_to_1_MUX__x2___74153 #(.Facing("east")) 4_to_1_mux_x2_74153_9: pin names not known; wires that end beside it: n4_to_1_mux_x2_74153_9_p1, n4_to_1_mux_x2_74153_9_p1, nor_3_out, 1'b0, and_32_out, and_37_out, and_21_out, or_1_out, 1'b0, 1'b0, and_24_out, A4, n4_to_1_mux_x2_74153_9_p13, n4_to_1_mux_x2_74153_9_p13, and_34_out, A5, n4_to_1_mux_x2_74153_9_p17, n4_to_1_mux_x2_74153_9_p18
  or or_15 (Z, n4_to_1_mux_x2_74153_9_p17, n4_to_1_mux_x2_74153_9_p18);

  assign Z_2 = Z;
endmodule
