// Logisim project part1.circ as structural Verilog: 1 circuit, main circuit main
module main (
  input  D,
  input  EN,
  output Q,
  output Q_bar
);

  wire nand_1_out, nand_2_out, not_1_out;

  not not_1 (not_1_out, D);
  nand nand_1 (nand_1_out, EN, not_1_out);
  nand nand_2 (nand_2_out, D, EN);
  nand nand_3 (Q, nand_2_out, Q_bar);
  nand nand_4 (Q_bar, Q, nand_1_out);
endmodule
