// Logisim project part3.circ as structural Verilog: 1 circuit, main circuit main
module main (
  input  D,
  input  CLK,
  input  CLR,
  input  PRE_bar,
  output Q,
  output Q_bar
);

  wire and_1_out, and_2_out, and_3_out, and_4_out, nand_1_out, nand_2_out, nand_3_out, nand_4_out,
       nand_5_out, nand_6_out, not_1_out, not_2_out, not_3_out, not_4_out, or_1_out;

  not not_1 (not_1_out, CLK);
  not not_2 (not_2_out, D);
  or or_1 (or_1_out, CLR, PRE_bar);
  nand nand_1 (nand_1_out, not_1_out, not_2_out);
  not not_3 (not_3_out, CLR);
  nand nand_2 (nand_2_out, D, not_1_out);
  and and_1 (and_1_out, nand_2_out, nand_4_out);
  and and_2 (and_2_out, nand_3_out, nand_1_out);
  nand nand_3 (nand_3_out, or_1_out, and_1_out);
  nand nand_4 (nand_4_out, and_2_out, not_3_out);
  not not_4 (not_4_out, nand_3_out);
  nand nand_5 (nand_5_out, nand_3_out, CLK);
  nand nand_6 (nand_6_out, CLK, not_4_out);
  and and_3 (and_3_out, Q, nand_6_out);
  and and_4 (and_4_out, nand_5_out, Q_bar);
  nand nand_7 (Q_bar, and_3_out, not_3_out);
  nand nand_8 (Q, or_1_out, and_4_out);
endmodule
