// Logisim project part4.circ as structural Verilog: 1 circuit, main circuit main
module main (
  input  CLK,
  input  CLR,
  input  J,
  input  PRE_bar,
  input  K,
  output Q,
  output Q_bar
);

  wire and_1_out, and_2_out, and_3_out, and_4_out, and_5_out, and_6_out, nand_1_out, nand_2_out, nand_3_out,
       nand_4_out, nand_5_out, nand_6_out, not_1_out, not_2_out, not_3_out, not_4_out, not_5_out, or_1_out,
       or_2_out;

  not not_1 (not_1_out, CLK);
  not not_2 (not_2_out, or_2_out);
  not not_3 (not_3_out, CLR);
  or or_1 (or_1_out, CLR, PRE_bar);
  nand nand_1 (nand_1_out, or_2_out, not_1_out);
  nand nand_2 (nand_2_out, not_1_out, not_2_out);
  or or_2 (or_2_out, and_3_out, and_4_out);
  and and_1 (and_1_out, nand_1_out, nand_4_out);
  and and_2 (and_2_out, nand_3_out, nand_2_out);
  and and_3 (and_3_out, Q_bar, J);
  and and_4 (and_4_out, not_4_out, Q);
  nand nand_3 (nand_3_out, or_1_out, and_1_out);
  nand nand_4 (nand_4_out, and_2_out, not_3_out);
  not not_4 (not_4_out, K);
  not not_5 (not_5_out, nand_3_out);
  nand nand_5 (nand_5_out, nand_3_out, CLK);
  nand nand_6 (nand_6_out, CLK, not_5_out);
  and and_5 (and_5_out, Q, nand_6_out);
  and and_6 (and_6_out, nand_5_out, Q_bar);
  nand nand_7 (Q, or_1_out, and_6_out);
  nand nand_8 (Q_bar, and_5_out, not_3_out);
endmodule
